# Fritzing sketch Diagrama electrico Caracterizacion temperatura (saved by Fritzing 0.9.5d)

parts:
  M1 = DOIT Esp32 DevKit v1 (30 pins long, 11 pins width) [part_number=ESP32S-PIN30]
  L298N1 = L298N DC motor driver
  M2 = DC Motor  # not connected
  DS1 = DS18B20 1-Wire Temperature Sensor Probe
  Q1 = NPN-Transistor [package="TO92 [THT]"]
  RY1 = SSR-50DA
  R1 = Resistor [tolerance=±5% resistance=4.7k package=THT]
  R2 = Resistor [tolerance=±5% resistance=220 package=THT]  # not connected
  VCC1 = Battery
  R3 = Resistor [tolerance=±5% resistance=220 package=THT]

nets:
  3V3: M1.3V3, DS1.VDD, R1.Pin_1
  GND: M1.GND, DS1.GND, VCC1.-
  N1: M1.D4, DS1.DQ, R1.Pin_0
  N2: M1.D25, L298N1.ENA
  N3: M1.D26, L298N1.IN1
  N4: M1.D27, L298N1.IN2
  N5: Q1.B, RY1.Pin_4
  N6: RY1.Pin_1, R3.Pin_0

notes:
  12V fuente ATX
  5V del cargador
  GND Fuente ATX
  5V Fuente ATX
  Fase 110V
  Neutro 110V
  Esp-32
  Driver L298N
  DS18B20
  SSR
  Resistencia de inmersion 800W

custom parts:
  DOIT Esp32 DevKit v1 (30 pins long, 11 pins width): The DOIT Esp32 DevKit v1 is one of the development board created by DOIT to evaluate the ESP-WROOM-32 module. It is based on the ESP32 microcontroller that boasts Wifi, Bluetooth, Ethernet and Low Power support all in a single chip. (vanepp) made breadboard work, adjusted pin numbering and labels and reduced size of schematic and cleaned up pcb. This chip is 30pins long (2 x15) and 11 pins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
  L298N DC motor driver: 2x DC motor driver with 78M05 positive voltage regulator (7..35 V) L298N: max 46 V, 2 A Set 5 V Enable jumper to enable 5 V regultor (needed for the L298N) and +5 V output at screw terminal or supply external +5 V at screw terminal Set ENA and/or ENB to +5 V to enable motor permanently or supply ENA and/or ENB with PWM signal IN1 and IN2 set rotation directory for motor A (OUT1/OUT2) IN2 and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
  SSR-50DA: SSR-50DA solid state relay.
